# Fritzing sketch MonkeyBox (saved by Fritzing 0.9.3b)
circuit board: 8.50402cm x 5.71915cm
breadboards: 1

parts:
  S1 = Toggle Switch [package=THT]  # not connected
  DFRobot_DFPlayer_Mini1 = DFRobot DFPlayer Mini [part_number=DFR0299]
  SP1 = SPEAKER [package=pcb_mount_speaker]  # not connected
  Part1 = Arduino Uno (Rev3) - ICSP
  J1_-_arm_servo = Basic Servo
  J2_-_lid_servo = Basic Servo
  R1 = Resistor [tolerance=±5% resistance=1k package=THT]
  J3_-_speaker = Screw terminal - 2 pins [package=THT]
  J4_-_switch = male pin header, 3 pins [form="♂ (male)"]

nets:
  VCC: DFRobot_DFPlayer_Mini1.VCC, Part1.5V, J1_-_arm_servo.vcc, J2_-_lid_servo.vcc, J4_-_switch.pin3
  N1: DFRobot_DFPlayer_Mini1.RX, R1.Pin_1
  N2: DFRobot_DFPlayer_Mini1.TX, Part1.D4
  N3: DFRobot_DFPlayer_Mini1.SPK_1, J3_-_speaker.pin2
  GND: DFRobot_DFPlayer_Mini1.GND-1, DFRobot_DFPlayer_Mini1.GND-2, Part1.GND, J1_-_arm_servo.gnd, J2_-_lid_servo.gnd, J4_-_switch.pin1
  N4: DFRobot_DFPlayer_Mini1.SPK_2, J3_-_speaker.pin1
  N5: DFRobot_DFPlayer_Mini1.BUSY, Part1.D6_PWM
  N6: Part1.D8, J4_-_switch.pin2
  N7: Part1.D3_PWM, J2_-_lid_servo.pulse
  N8: Part1.D5_PWM, J1_-_arm_servo.pulse
  N9: Part1.D7, R1.Pin_0
